// Logisim project 4 bit processor logisim 2.circ as structural Verilog: 6 circuits, main circuit Main
module main (
  input  [3:0] in_1,
  input  [3:0] in_2,
  input  [3:0] in_3,
  output [3:0] out_4
);

  // MIPS_ALU_4_bit mips_alu_4_bit_1: pin names not known; wires that end beside it: in_1, in_2, in_3, out_4
endmodule

module Control (
  input  [3:0] Opcode,
  output RegWrite,
  output ALUSrc,
  output MemWrite,
  output [3:0] ALUOP,
  output MemToReg,
  output MemRead,
  output Branch,
  output Jump,
  output RegDst
);

  ROM #(.addrWidth(4), .dataWidth(12)) rom_1 (
    .addr(Opcode), .data({RegDst, Jump, Branch, MemRead, MemToReg, ALUOP, MemWrite, ALUSrc, RegWrite}));  // open: sel

  // Notes on the sheet:
  //   contents of rom_1 (hex, n*v repeats v):
  //   0 33 801 3 809 193 16 811 400 13 831 b 230
endmodule

module Splitter (
  input  [15:0] Instruction_Set,
  output [3:0] OpCode,
  output [2:0] rs,
  output [2:0] rt,
  output [2:0] rd,
  output [3:0] Offset_Immidiate,
  output [3:0] Address
);


  assign Address = Instruction_Set[11:8];
  assign Offset_Immidiate = Instruction_Set[5:2];
  assign OpCode = Instruction_Set[15:12];
  assign rd = Instruction_Set[5:3];
  assign rs = Instruction_Set[11:9];
  assign rt = Instruction_Set[8:6];
endmodule

module Registers (
  input  RegClock,
  input  RegWrite,
  input  [2:0] ReadReg1,
  input  [2:0] WriteReg,
  input  [2:0] ReadReg2,
  input  [3:0] WriteData,
  output [3:0] ReadData1,
  output [3:0] ReadData2
);

  wire and_1_out, and_2_out, and_3_out, and_4_out, and_5_out, and_6_out, and_7_out, and_8_out,
       decoder_1_out0, decoder_1_out1, decoder_1_out2, decoder_1_out3, decoder_1_out4, decoder_1_out5,
       decoder_1_out6, decoder_1_out7;
  wire [3:0] register_1_q, register_2_q, register_3_q, register_4_q, register_5_q, register_6_q,
       register_7_q, register_8_q;

  Decoder #(.select(3)) decoder_1 (
    .out0(decoder_1_out0), .out1(decoder_1_out1), .out2(decoder_1_out2), .out3(decoder_1_out3),
    .out4(decoder_1_out4), .out5(decoder_1_out5), .out6(decoder_1_out6), .out7(decoder_1_out7), .sel(WriteReg));  // open: en
  and and_1 (and_1_out, decoder_1_out0, RegWrite);
  and and_2 (and_2_out, decoder_1_out1, RegWrite);
  and and_3 (and_3_out, decoder_1_out2, RegWrite);
  and and_4 (and_4_out, decoder_1_out3, RegWrite);
  and and_5 (and_5_out, decoder_1_out4, RegWrite);
  and and_6 (and_6_out, decoder_1_out5, RegWrite);
  and and_7 (and_7_out, decoder_1_out6, RegWrite);
  and and_8 (and_8_out, decoder_1_out7, RegWrite);
  // main main_1: pin names not known; wires that end beside it: and_8_out, and_7_out, and_6_out
  Register #(.width(4)) register_1 (.D(WriteData), .en(and_1_out), .Q(register_1_q), .clk(RegClock));  // open: clr
  Register #(.width(4)) register_2 (.D(WriteData), .en(and_5_out), .Q(register_2_q), .clk(RegClock));  // open: clr
  Register #(.width(4)) register_3 (.D(WriteData), .en(and_2_out), .Q(register_3_q), .clk(RegClock));  // open: clr
  Register #(.width(4)) register_4 (.D(WriteData), .en(and_6_out), .Q(register_4_q), .clk(RegClock));  // open: clr
  Register #(.width(4)) register_5 (.D(WriteData), .en(and_3_out), .Q(register_5_q), .clk(RegClock));  // open: clr
  Register #(.width(4)) register_6 (.D(WriteData), .en(and_7_out), .Q(register_6_q), .clk(RegClock));  // open: clr
  Register #(.width(4)) register_7 (.D(WriteData), .en(and_4_out), .Q(register_7_q), .clk(RegClock));  // open: clr
  Register #(.width(4)) register_8 (.D(WriteData), .en(and_8_out), .Q(register_8_q), .clk(RegClock));  // open: clr
  Multiplexer #(.select(3), .width(4)) multiplexer_1 (
    .in0(register_1_q), .in1(register_3_q), .in2(register_5_q), .in3(register_7_q), .in4(register_2_q),
    .in5(register_4_q), .in6(register_6_q), .in7(register_8_q), .out(ReadData1), .sel(ReadReg1));  // open: en
  Multiplexer #(.select(3), .width(4)) multiplexer_2 (
    .in0(register_1_q), .in1(register_3_q), .in2(register_5_q), .in3(register_7_q), .in4(register_2_q),
    .in5(register_4_q), .in6(register_6_q), .in7(register_8_q), .out(ReadData2), .sel(ReadReg2));  // open: en
endmodule

module Main (
  input  [3:0] in_1,
  output [3:0] out_2,
  output [3:0] out_3,
  output [3:0] out_4,
  output [3:0] out_5,
  output [3:0] out_6,
  output [3:0] out_7,
  output out_8,
  output [3:0] out_9
);

  wire and_1_out, Control_alusrc, Control_branch, Control_jump, Control_memread, Control_memwrite,
       Control_regdst, Control_regwrite, Main_Clock_out, mips_alu_4_bit_1_p4;
  wire [2:0] multiplexer_1_out, splitter_1_rd, splitter_1_rs, splitter_1_rt;
  wire [3:0] adder_1_out, adder_2_out, multiplexer_3_out, PC_q, ram_2_data, Reg_readdata2,
       splitter_1_address, splitter_1_offset_immidiate, splitter_1_opcode;
  wire [15:0] ram_1_data;

  Register #(.width(4)) PC (.D(out_2), .Q(PC_q), .clk(Main_Clock_out));  // open: en, clr
  Clock Main_Clock (.out(Main_Clock_out));
  Adder #(.width(4)) adder_1 (.a(in_1), .b(PC_q), .out(adder_1_out));  // open: cin, cout
  RAM #(.addrWidth(4), .dataWidth(16)) ram_1 (.addr(PC_q), .data(ram_1_data));  // open: sel, clk, ld, clr
  Splitter splitter_1 (
    .Instruction_Set(ram_1_data), .OpCode(splitter_1_opcode), .rs(splitter_1_rs), .rt(splitter_1_rt),
    .rd(splitter_1_rd), .Offset_Immidiate(splitter_1_offset_immidiate), .Address(splitter_1_address));
  Control Control (
    .Opcode(splitter_1_opcode), .RegWrite(Control_regwrite), .ALUSrc(Control_alusrc),
    .MemWrite(Control_memwrite), .ALUOP(out_7), .MemToReg(out_8), .MemRead(Control_memread),
    .Branch(Control_branch), .Jump(Control_jump), .RegDst(Control_regdst));
  Multiplexer #(.width(3)) multiplexer_1 (
    .in0(splitter_1_rd), .in1(splitter_1_rt), .out(multiplexer_1_out), .sel(Control_regdst));  // open: en
  Registers Reg (
    .RegClock(Main_Clock_out), .RegWrite(Control_regwrite), .WriteReg(multiplexer_1_out),
    .ReadReg2(splitter_1_rt), .WriteData(out_9), .ReadData1(out_3), .ReadReg1(splitter_1_rs),
    .ReadData2(Reg_readdata2));
  Multiplexer #(.width(4)) multiplexer_2 (
    .in0(Reg_readdata2), .in1(splitter_1_offset_immidiate), .out(out_6), .sel(Control_alusrc));  // open: en
  Adder #(.width(4)) adder_2 (.a(splitter_1_offset_immidiate), .b(adder_1_out), .out(adder_2_out));  // open: cin, cout
  // MIPS_ALU_4_bit mips_alu_4_bit_1: pin names not known; wires that end beside it: out_3, out_6, out_7, mips_alu_4_bit_1_p4, out_4
  Multiplexer #(.width(4)) multiplexer_3 (
    .in0(adder_1_out), .in1(adder_2_out), .out(multiplexer_3_out), .sel(and_1_out));  // open: en
  and and_1 (and_1_out, Control_branch, mips_alu_4_bit_1_p4);
  Multiplexer #(.width(4)) multiplexer_4 (
    .in0(multiplexer_3_out), .in1(splitter_1_address), .out(out_2), .sel(Control_jump));  // open: en
  RAM #(.addrWidth(4), .dataWidth(4), .bus("separate")) ram_2 (
    .addr(out_4), .din(Reg_readdata2), .data(ram_2_data), .str(Control_memwrite), .clk(Main_Clock_out),
    .ld(Control_memread));  // open: sel, clr
  Multiplexer #(.width(4)) multiplexer_5 (.in0(out_4), .in1(ram_2_data), .out(out_9), .sel(out_8));  // open: en

  assign out_5 = out_3;
endmodule

module regfile (
  input  RegClock,
  input  RegWrite5,
  input  [2:0] ReadReg1,
  input  [2:0] WriteReg,
  input  [2:0] ReadReg2,
  input  [3:0] WriteData,
  output [3:0] ReadData1,
  output [3:0] ReadData2
);

  wire and_1_out, and_2_out, and_3_out, and_4_out, and_5_out, and_6_out, and_7_out, and_8_out,
       decoder_1_out0, decoder_1_out1, decoder_1_out2, decoder_1_out3, decoder_1_out4, decoder_1_out5,
       decoder_1_out6, decoder_1_out7;
  wire [3:0] register_1_q, register_2_q, register_3_q, register_4_q, register_5_q, register_6_q,
       register_7_q, register_8_q;

  Decoder #(.select(3)) decoder_1 (
    .out0(decoder_1_out0), .out1(decoder_1_out1), .out2(decoder_1_out2), .out3(decoder_1_out3),
    .out4(decoder_1_out4), .out5(decoder_1_out5), .out6(decoder_1_out6), .out7(decoder_1_out7),
    .sel(WriteReg), .en(1'b1));
  and and_1 (and_1_out, decoder_1_out0, RegWrite5);
  and and_2 (and_2_out, decoder_1_out1, RegWrite5);
  and and_3 (and_3_out, decoder_1_out2, RegWrite5);
  and and_4 (and_4_out, decoder_1_out3, RegWrite5);
  and and_5 (and_5_out, decoder_1_out4, RegWrite5);
  and and_6 (and_6_out, decoder_1_out5, RegWrite5);
  and and_7 (and_7_out, decoder_1_out6, RegWrite5);
  and and_8 (and_8_out, decoder_1_out7, RegWrite5);
  // main main_1: pin names not known; wires that end beside it: and_8_out, and_7_out, and_6_out
  Register #(.width(4)) register_1 (.D(WriteData), .en(and_1_out), .Q(register_1_q), .clk(RegClock));  // open: clr
  Register #(.width(4)) register_2 (.D(WriteData), .en(and_5_out), .Q(register_2_q), .clk(RegClock));  // open: clr
  Register #(.width(4)) register_3 (.D(WriteData), .en(and_2_out), .Q(register_3_q), .clk(RegClock));  // open: clr
  Register #(.width(4)) register_4 (.D(WriteData), .en(and_6_out), .Q(register_4_q), .clk(RegClock));  // open: clr
  Register #(.width(4)) register_5 (.D(WriteData), .en(and_3_out), .Q(register_5_q), .clk(RegClock));  // open: clr
  Register #(.width(4)) register_6 (.D(WriteData), .en(and_7_out), .Q(register_6_q), .clk(RegClock));  // open: clr
  Register #(.width(4)) register_7 (.D(WriteData), .en(and_4_out), .Q(register_7_q), .clk(RegClock));  // open: clr
  Register #(.width(4)) register_8 (.D(WriteData), .en(and_8_out), .Q(register_8_q), .clk(RegClock));  // open: clr
  Multiplexer #(.select(3), .width(4)) multiplexer_1 (
    .in0(register_1_q), .in1(register_3_q), .in2(register_5_q), .in3(register_7_q), .in4(register_2_q),
    .in5(register_4_q), .in6(register_6_q), .in7(register_8_q), .out(ReadData1), .sel(ReadReg1), .en(1'b1));
  Multiplexer #(.select(3), .width(4)) multiplexer_2 (
    .in0(register_1_q), .in1(register_3_q), .in2(register_5_q), .in3(register_7_q), .in4(register_2_q),
    .in5(register_4_q), .in6(register_6_q), .in7(register_8_q), .out(ReadData2), .sel(ReadReg2), .en(1'b1));
endmodule
