// Logisim project 4 bit processor logisim.circ as structural Verilog: 4 circuits, main circuit main
module main (
);

  Splitter splitter_1 ();  // open: Instruction_Set, OpCode, rs, rt, rd, Offset_Immidiate, Address
  Control Control_CKT ();  // open: Opcode, RegWrite, ALUSrc, MemWrite, ALUOP, MemToReg, MemRead, Branch, Jump, RegDst
endmodule

module Control (
  input  [3:0] Opcode,
  output RegWrite,
  output ALUSrc,
  output MemWrite,
  output [1:0] ALUOP,
  output MemToReg,
  output MemRead,
  output Branch,
  output Jump,
  output RegDst
);

  wire [11:10] rom_1_data;

  ROM #(.addrWidth(4), .dataWidth(12)) rom_1 (
    .addr(Opcode),
    .data({rom_1_data, RegDst, Jump, Branch, MemRead, MemToReg, ALUOP, MemWrite, ALUSrc, RegWrite}));  // open: sel

  // Notes on the sheet:
  //   contents of rom_1 (hex, n*v repeats v):
  //   0 3 209 b 211 63 6 219 100 1b 201 13 88
endmodule

module Splitter (
  input  [15:0] Instruction_Set,
  output [3:0] OpCode,
  output [2:0] rs,
  output [2:0] rt,
  output [2:0] rd,
  output [3:0] Offset_Immidiate,
  output [11:0] Address
);


  assign Address = Instruction_Set[11:0];
  assign Offset_Immidiate = Instruction_Set[5:2];
  assign OpCode = Instruction_Set[15:12];
  assign rd = Instruction_Set[5:3];
  assign rs = Instruction_Set[11:9];
  assign rt = Instruction_Set[8:6];
endmodule

module Registers (
  input  Reg_Clock,
  input  Reg_Write,
  input  [2:0] Read_Reg_1,
  input  [2:0] Write_Reg,
  input  [2:0] Read_Reg_2,
  input  [3:0] Write_Data,
  output [3:0] Read_Data_1,
  output [3:0] Read_Data_2
);

  wire and_1_out, and_2_out, and_3_out, and_4_out, and_5_out, and_6_out, and_7_out, and_8_out,
       decoder_1_out0, decoder_1_out1, decoder_1_out2, decoder_1_out3, decoder_1_out4, decoder_1_out5,
       decoder_1_out6, decoder_1_out7;
  wire [3:0] register_1_q, register_2_q, register_3_q, register_4_q, register_5_q, register_6_q,
       register_7_q, register_8_q;

  Decoder #(.select(3)) decoder_1 (
    .out0(decoder_1_out0), .out1(decoder_1_out1), .out2(decoder_1_out2), .out3(decoder_1_out3),
    .out4(decoder_1_out4), .out5(decoder_1_out5), .out6(decoder_1_out6), .out7(decoder_1_out7),
    .sel(Write_Reg), .en(1'b1));
  and and_1 (and_1_out, decoder_1_out0, Reg_Write);
  and and_2 (and_2_out, decoder_1_out1, Reg_Write);
  and and_3 (and_3_out, decoder_1_out2, Reg_Write);
  and and_4 (and_4_out, decoder_1_out3, Reg_Write);
  and and_5 (and_5_out, decoder_1_out4, Reg_Write);
  and and_6 (and_6_out, decoder_1_out5, Reg_Write);
  and and_7 (and_7_out, decoder_1_out6, Reg_Write);
  and and_8 (and_8_out, decoder_1_out7, Reg_Write);
  main main_1 ();
  Register #(.width(4)) register_1 (.D(Write_Data), .en(and_1_out), .Q(register_1_q), .clk(Reg_Clock));  // open: clr
  Register #(.width(4)) register_2 (.D(Write_Data), .en(and_5_out), .Q(register_2_q), .clk(Reg_Clock));  // open: clr
  Register #(.width(4)) register_3 (.D(Write_Data), .en(and_2_out), .Q(register_3_q), .clk(Reg_Clock));  // open: clr
  Register #(.width(4)) register_4 (.D(Write_Data), .en(and_6_out), .Q(register_4_q), .clk(Reg_Clock));  // open: clr
  Register #(.width(4)) register_5 (.D(Write_Data), .en(and_3_out), .Q(register_5_q), .clk(Reg_Clock));  // open: clr
  Register #(.width(4)) register_6 (.D(Write_Data), .en(and_7_out), .Q(register_6_q), .clk(Reg_Clock));  // open: clr
  Register #(.width(4)) register_7 (.D(Write_Data), .en(and_4_out), .Q(register_7_q), .clk(Reg_Clock));  // open: clr
  Register #(.width(4)) register_8 (.D(Write_Data), .en(and_8_out), .Q(register_8_q), .clk(Reg_Clock));  // open: clr
  Multiplexer #(.select(3), .width(4)) multiplexer_1 (
    .in0(register_1_q), .in1(register_3_q), .in2(register_5_q), .in3(register_7_q), .in4(register_2_q),
    .in5(register_4_q), .in6(register_6_q), .in7(register_8_q), .out(Read_Data_1), .sel(Read_Reg_1), .en(1'b1));
  Multiplexer #(.select(3), .width(4)) multiplexer_2 (
    .in0(register_1_q), .in1(register_3_q), .in2(register_5_q), .in3(register_7_q), .in4(register_2_q),
    .in5(register_4_q), .in6(register_6_q), .in7(register_8_q), .out(Read_Data_2), .sel(Read_Reg_2), .en(1'b1));
endmodule
